# Fritzing sketch server-with-relay (saved by Fritzing 0.9.3b)

parts:
  U1 = ESP32-38PinWide [part_number=ESP32-38PinWide]
  Switch-Manual = Toggle Switch [package=THT]
  Switch-Mode = Toggle Switch [package=THT]
  U3 = RELAY [package=relay-g5q]
  M1 = DC Motor
  220v_AC_to_5v_DC = HLK-PM01
  R1 = Resistor [tolerance=±5% resistance=220 package=THT]

nets:
  N1: U1.GPIO33, R1.Pin_0
  N2: U1.GPIO25, Switch-Manual.COM, U3.COIL2
  N3: U1.GND, 220v_AC_to_5v_DC.-Vo
  N4: U1.VIN, Switch-Mode.L2, 220v_AC_to_5v_DC.+Vo
  N5: Switch-Manual.L2, Switch-Mode.COM, R1.Pin_1
  N6: U3.MAIN, 220v_AC_to_5v_DC.AC#1
  N7: U3.NO, M1.pin_1
  N8: M1.pin_2, 220v_AC_to_5v_DC.AC#0

custom parts:
  ESP32-38PinWide: Generic 38-Pin ESP32 with wide format (only access to one side of pins on a breadboard) based on Stephen Lilley's HiLetgo ESP-WROOM-32 ESP32 ESP-32S Development Board.
